# Fritzing sketch Schema_nano (saved by Fritzing 0.9.3b)
circuit board: 12.2649cm x 9.30836cm

parts:
  Composant5 = Arduino Nano (Rev3.0)
  S8 = Pushbutton [package="[THT]"]
  S9 = Pushbutton [package="[THT]"]
  S10 = Pushbutton [package="[THT]"]
  S11 = Pushbutton [package="[THT]"]
  S12 = Pushbutton [package="[THT]"]
  S13 = Pushbutton [package="[THT]"]
  S14 = Pushbutton [package="[THT]"]
  Composant7 = Triple Axis Accelerometer Breakout - ADXL335

nets:
  GND: Composant5.GND, S8.Pin_1, S8.Pin_2, S9.Pin_3, S9.Pin_4, S10.Pin_3, S10.Pin_4, S11.Pin_3, S12.Pin_3, S12.Pin_4, S13.Pin_4, S14.Pin_3, S14.Pin_4, Composant7.GND
  N1: Composant5.D2, S13.Pin_1, S13.Pin_2
  N2: Composant5.D3, S9.Pin_1, S9.Pin_2
  N3: Composant5.D4, S8.Pin_3, S8.Pin_4
  N4: Composant5.D5, S10.Pin_1, S10.Pin_2
  N5: Composant5.D6, S12.Pin_1, S12.Pin_2
  N6: Composant5.D7, S11.Pin_1, S11.Pin_2
  N7: Composant5.D8, S14.Pin_1, S14.Pin_2
  N8: Composant5.A2, Composant7.ZOUT
  N9: Composant5.A1, Composant7.YOUT
  N10: Composant5.A0, Composant7.XOUT
  3V3: Composant5.3V3, Composant7.VCC
